// Logisim project Cerradura.circ as structural Verilog: 1 circuit, main circuit main
module main (
  input  A,
  input  B
);

  wire and_1_out, and_2_out, and_3_out, and_4_out, and_5_out, and_6_out, clock_1_out, d_ff_1_q, d_ff_2_q,
       not_1_out, not_2_out, not_3_out, not_4_out, not_5_out, or_1_out, or_2_out;

  not not_1 (not_1_out, A);
  not not_2 (not_2_out, B);
  not not_3 (not_3_out, d_ff_1_q);
  not not_4 (not_4_out, d_ff_2_q);
  not not_5 (not_5_out, A);
  and and_1 (and_1_out, not_5_out, d_ff_1_q);
  and and_2 (and_2_out, A, d_ff_2_q);
  and and_3 (and_3_out, not_1_out, not_2_out, d_ff_2_q);
  and and_4 (and_4_out, B, d_ff_1_q);
  and and_5 (and_5_out, A, not_3_out, not_4_out);
  or or_1 (or_1_out, and_1_out, and_2_out);
  or or_2 (or_2_out, and_3_out, and_4_out, and_5_out);
  Clock clock_1 (.out(clock_1_out));
  D_Flip_Flop d_ff_1 (.D(or_1_out), .clk(clock_1_out), .Q(d_ff_1_q));  // open: Qn, preset, reset
  D_Flip_Flop d_ff_2 (.D(or_2_out), .clk(clock_1_out), .Q(d_ff_2_q));  // open: Qn, preset, reset
  and and_6 (and_6_out, B, d_ff_1_q);
  LED led_1 (.in(and_6_out));

  // Notes on the sheet:
  //   Combinacion Correcta AAB
  //   Cerradura de puerta
endmodule
